# Fritzing sketch proto_demo_simon3 (saved by Fritzing 1.0.3b)
circuit board: 6.88566cm x 5.36311cm
breadboards: 1
perfboards: 1

parts:
  S1 = Pushbutton [package="[THT]"]
  0 = Arduino Prototyping Shield
  LED2 = LED - 3mm [color="Yellow (585nm)" current=0.030A package="3 mm [THT]"]
  LED1 = LED - 3mm [color="Red (633nm)" current=0.030A package="3 mm [THT]"]
  LED3 = LED - 3mm [color="Green (560nm)" current=0.030A package="3 mm [THT]"]
  R1 = Resistor [tolerance=±5% power=0.25W resistance=470 package=THT]
  R2 = Resistor [tolerance=±5% power=0.25W resistance=470 package=THT]
  R3 = Resistor [tolerance=±5% power=0.25W resistance=470 package=THT]
  S2 = Pushbutton [package="[THT]"]
  S3 = Pushbutton [package="[THT]"]

nets (from the pcb view):
  N1: S1.Pin_1, S1.Pin_2, 0.D12
  N2: S1.Pin_3, S1.Pin_4, 0.GND, LED2.cathode, LED1.cathode, LED3.cathode, S2.Pin_3, S2.Pin_4, S3.Pin_3
  N3: 0.A0, R1.Pin_1
  N4: 0.A1, R2.Pin_1
  N5: 0.A2, R3.Pin_1
  N6: 0.D3, S3.Pin_1, S3.Pin_2
  N7: 0.D8, S2.Pin_1, S2.Pin_2
  N8: LED2.anode, R2.Pin_0
  N9: LED1.anode, R1.Pin_0
  N10: LED3.anode, R3.Pin_0
